# Fritzing sketch Fritzing Sketch (saved by Fritzing 0.9.2b)

parts:
  Raspberry_Pi1 = Raspberry Pi 2
  GPS1 = Adafruit Ultimate GPS Breakout

nets:
  N1: Raspberry_Pi1.GPIO15, GPS1.TX
  N2: Raspberry_Pi1.GPIO14, GPS1.RX
  GND: Raspberry_Pi1.GND, GPS1.GND
  5V: Raspberry_Pi1.5V, GPS1.VIN
